// Digital circuit Digital3.dig as structural Verilog
module Digital3 (
  input  A,
  input  B,
  input  C,
  output Y
);

  wire not_1_out, not_2_out, not_3_out;

  not not_1 (not_1_out, A);
  not not_2 (not_2_out, B);
  not not_3 (not_3_out, C);
  or or_1 (Y, not_1_out, not_2_out, not_3_out);
endmodule
