// Digital circuit Digital4.dig as structural Verilog
module Digital4 (
  input  A,
  input  B,
  input  C,
  output Y
);

  wire and_1_out, and_2_out, and_3_out, nand_1_out, nand_2_out, nand_3_out, not_1_out;

  not not_1 (not_1_out, C);
  nand nand_1 (nand_1_out, A, B, C);
  nand nand_2 (nand_2_out, A, B);
  nand nand_3 (nand_3_out, B, C);
  and and_1 (and_1_out, A, B, not_1_out);
  and and_2 (and_2_out, nand_2_out, C);
  and and_3 (and_3_out, A, nand_3_out);
  or or_1 (Y, nand_1_out, and_2_out, and_3_out, and_1_out);
endmodule
